// Logisim project ТА2.circ as structural Verilog: 4 circuits, main circuit main
// ИП
module \Без_имени  (
  input  a,
  input  b,
  input  c,
  input  d,
  output f1,
  output f2,
  output f3,
  output f4,
  output f5,
  output f6,
  output f7
);

  wire and_1_out, and_2_out, and_3_out, and_4_out, and_5_out, and_6_out, and_7_out, and_8_out, and_9_out,
       and_10_out, and_11_out, and_12_out, and_13_out, and_14_out, and_15_out, not_1_out, not_2_out,
       not_3_out, not_4_out, not_5_out, not_6_out, not_7_out, not_8_out, not_9_out, not_10_out, not_11_out,
       not_12_out, not_13_out, not_14_out, not_15_out;

  not not_1 (not_1_out, b);
  and and_1 (and_1_out, not_1_out, c);
  and and_2 (and_2_out, b, not_2_out);
  not not_2 (not_2_out, c);
  and and_3 (and_3_out, b, not_3_out);
  not not_3 (not_3_out, d);
  and and_4 (and_4_out, b, not_4_out);
  not not_4 (not_4_out, c);
  and and_5 (and_5_out, b, not_5_out);
  not not_5 (not_5_out, d);
  and and_6 (and_6_out, b, d);
  not not_6 (not_6_out, a);
  and and_7 (and_7_out, not_6_out, not_7_out, d);
  not not_7 (not_7_out, b);
  not not_8 (not_8_out, b);
  and and_8 (and_8_out, not_8_out, c);
  and and_9 (and_9_out, c, d);
  not not_9 (not_9_out, c);
  and and_10 (and_10_out, b, not_9_out, not_10_out);
  not not_10 (not_10_out, d);
  and and_11 (and_11_out, a, not_11_out);
  not not_11 (not_11_out, d);
  and and_12 (and_12_out, c, not_12_out);
  not not_12 (not_12_out, d);
  not not_13 (not_13_out, b);
  and and_13 (and_13_out, not_13_out, c);
  and and_14 (and_14_out, c, not_14_out);
  not not_14 (not_14_out, d);
  not not_15 (not_15_out, c);
  and and_15 (and_15_out, b, not_15_out, d);
  or or_1 (f7, d, b, a);
  or or_2 (f1, and_1_out, and_2_out, and_3_out, a);
  or or_3 (f2, and_4_out, and_5_out, a);
  or or_4 (f3, c, and_6_out, a);
  or or_5 (f4, and_7_out, and_8_out, and_9_out, and_10_out, and_11_out);
  or or_6 (f5, and_12_out, a);
  or or_7 (f6, and_13_out, and_14_out, and_15_out, a);
endmodule

module main (
  input  in_1,
  input  in_2,
  input  in_3,
  input  in_4,
  input  in_5,
  output AM,
  output PM,
  output out_8,
  output out_9,
  output out_10,
  output out_11,
  output out_12,
  output out_13,
  output out_14
);

  wire and_1_out, and_2_out, and_3_out, and_4_out, and_5_out, and_7_out, and_8_out, and_9_out, and_10_out,
       and_11_out, and_12_out, and_13_out, and_14_out, and_15_out, and_16_out, and_18_out, and_19_out,
       and_20_out, and_21_out, and_22_out, and_23_out, and_24_out, and_25_out, and_26_out, and_27_out,
       and_28_out, and_29_out, and_30_out, and_37_out, clock_1_out, controlled_buffer_18_out,
       controlled_buffer_19_out, counter_1_q, counter_13_q, H, L1, L2, L3, L4, L5, not_1_out, not_2_out,
       not_4_out, not_5_out, not_6_out, not_7_out, or_1_out, or_2_out, or_3_out, or_4_out, or_5_out,
       or_6_out, or_7_out, or_8_out, or_9_out, or_10_out, or_11_out, or_12_out, Q1, Q1_2_out, Q1_out, Q2,
       Q2_out, Q3, Q3_out, T2, T3, \ВЫХ_СБ , \ЗВУК , \КП1ВЫХ , \КП2ВЫХ , \КП3ВЫХ , \КП4ВЫХ , \КП5ВЫХ ,
       \КП6ВЫХ , \КП7ВЫХ , \КП11ВЫХ , \КП22ВЫХ , \КП33ВЫХ , \КП44ВЫХ ;
  wire [2:0] \В2 , \В4 , \В6 , \В8 , \ип_1_f7 , \ип_2_f7 , \ип_3_f7 , \ип_4_f7 ;
  wire [3:0] controlled_buffer_2_out, controlled_buffer_6_out, controlled_buffer_9_out,
       controlled_buffer_15_out, \В , \В3 , \В5 , \В7 , \ИП1 , \ИП2 , \ИП3 , \ИП4 , \ИП5 , \ИП6 , \ИП7 ,
       \ИП8 , \ИП9 , \ип_1_f4 , \ип_2_f4 , \ип_3_f4 , \ип_4_f4 , \КП1 , \КП2 ;

  or or_1 (or_1_out, in_4, in_1);
  or or_2 (or_2_out, in_2, in_4);
  _7_Segment_Display u_7_segment_display_1 (
    .g(\В7 [3]), .f(\В7 [2]), .a(\В7 [1]), .b(\В7 [0]), .e(\В8 [2]), .d(\В8 [1]), .c(\В8 [0]));  // open: dp
  Counter #(.width(1), .max('h1)) counter_1 (.Q(counter_1_q), .clk(in_5));  // open: load, D, count, carry, clr
  not not_1 (not_1_out, counter_1_q);
  _7_Segment_Display u_7_segment_display_2 (
    .g(\В5 [3]), .f(\В5 [2]), .a(\В5 [1]), .b(\В5 [0]), .e(\В6 [2]), .d(\В6 [1]), .c(\В6 [0]));  // open: dp
  and and_1 (and_1_out, L1, not_1_out);
  assign \В7  = and_1_out ? \ип_1_f4  : 4'bz;  // Controlled_Buffer controlled_buffer_1
  \ИП  \u_ип_1  (
    .a(controlled_buffer_2_out[3]), .b(controlled_buffer_2_out[2]), .c(controlled_buffer_2_out[1]),
    .d(controlled_buffer_2_out[0]), .f1(\ип_1_f4 [3]), .f2(\ип_1_f4 [2]), .f3(\ип_1_f4 [1]),
    .f4(\ип_1_f4 [0]), .f5(\ип_1_f7 [2]), .f6(\ип_1_f7 [1]), .f7(\ип_1_f7 [0]));
  assign controlled_buffer_2_out = not_2_out ? \ИП4  : 4'bz;  // Controlled_Buffer controlled_buffer_2
  and and_2 (and_2_out, not_1_out, L3);
  assign controlled_buffer_2_out = L4 ? \ИП9  : 4'bz;  // Controlled_Buffer controlled_buffer_3
  _7_Segment_Display u_7_segment_display_3 (
    .g(\В3 [3]), .f(\В3 [2]), .a(\В3 [1]), .b(\В3 [0]), .e(\В4 [2]), .d(\В4 [1]), .c(\В4 [0]));  // open: dp
  assign \В8  = and_1_out ? \ип_1_f7  : 3'bz;  // Controlled_Buffer controlled_buffer_4
  assign \В5  = and_1_out ? \ип_2_f4  : 4'bz;  // Controlled_Buffer controlled_buffer_5
  \ИП  \u_ип_2  (
    .a(controlled_buffer_6_out[3]), .b(controlled_buffer_6_out[2]), .c(controlled_buffer_6_out[1]),
    .d(controlled_buffer_6_out[0]), .f1(\ип_2_f4 [3]), .f2(\ип_2_f4 [2]), .f3(\ип_2_f4 [1]),
    .f4(\ип_2_f4 [0]), .f5(\ип_2_f7 [2]), .f6(\ип_2_f7 [1]), .f7(\ип_2_f7 [0]));
  assign controlled_buffer_6_out = not_2_out ? \ИП3  : 4'bz;  // Controlled_Buffer controlled_buffer_6
  assign controlled_buffer_6_out = L4 ? \ИП8  : 4'bz;  // Controlled_Buffer controlled_buffer_7
  _7_Segment_Display u_7_segment_display_4 (
    .g(\В [3]), .f(\В [2]), .a(\В [1]), .b(\В [0]), .e(\В2 [2]), .d(\В2 [1]), .c(\В2 [0]));  // open: dp
  assign \В6  = and_1_out ? \ип_2_f7  : 3'bz;  // Controlled_Buffer controlled_buffer_8
  \ИП  \u_ип_3  (
    .a(controlled_buffer_9_out[3]), .b(controlled_buffer_9_out[2]), .c(controlled_buffer_9_out[1]),
    .d(controlled_buffer_9_out[0]), .f1(\ип_3_f4 [3]), .f2(\ип_3_f4 [2]), .f3(\ип_3_f4 [1]),
    .f4(\ип_3_f4 [0]), .f5(\ип_3_f7 [2]), .f6(\ип_3_f7 [1]), .f7(\ип_3_f7 [0]));
  assign controlled_buffer_9_out = L4 ? \ИП7  : 4'bz;  // Controlled_Buffer controlled_buffer_9
  and and_3 (and_3_out, or_2_out, ~L4, ~T2, ~T3);  // AND_Gate
  and and_4 (and_4_out, or_2_out, L4, T2);
  and and_5 (and_5_out, or_1_out, L4);
  // AND_Gate and_6 has open pins: in0=or_2_out, in1=L4, in2=T2, out=open
  and and_7 (and_7_out, or_1_out, T2, ~T3);  // AND_Gate
  and and_8 (and_8_out, or_1_out, or_2_out, T2);
  and and_9 (and_9_out, or_2_out, ~L4, T2);  // AND_Gate
  and and_10 (and_10_out, or_1_out, ~or_2_out, L4, T3);  // AND_Gate
  and and_11 (and_11_out, or_1_out, ~or_2_out, ~T2, T3);  // AND_Gate
  and and_12 (and_12_out, or_1_out, or_2_out, T3);
  and and_13 (and_13_out, or_2_out, ~L4, T3);  // AND_Gate
  and and_14 (and_14_out, or_1_out, ~or_2_out, T2, ~T3);  // AND_Gate
  and and_15 (and_15_out, or_1_out, ~L4, ~T2, ~T3);  // AND_Gate
  and and_16 (and_16_out, ~or_1_out, or_2_out, L4, T2);  // AND_Gate
  // AND_Gate and_17 has open pins: in0=or_1_out, in1=or_2_out, in2=L4, in3=T2, in4=T3, out=open
  and and_18 (and_18_out, or_1_out, ~or_2_out, ~L4, ~T2, ~T3);  // AND_Gate
  and and_19 (and_19_out, or_1_out, ~or_2_out, L4, T3);  // AND_Gate
  and and_20 (and_20_out, or_1_out, ~or_2_out, L4, T2);  // AND_Gate
  and and_21 (and_21_out, ~or_1_out, or_2_out, L4, T2, ~T3);  // AND_Gate
  assign \В3  = and_22_out ? \ип_3_f4  : 4'bz;  // Controlled_Buffer controlled_buffer_10
  assign \В4  = and_22_out ? \ип_3_f7  : 3'bz;  // Controlled_Buffer controlled_buffer_11
  \ИП  \u_ип_4  (
    .a(controlled_buffer_15_out[3]), .b(controlled_buffer_15_out[2]), .c(controlled_buffer_15_out[1]),
    .d(controlled_buffer_15_out[0]), .f1(\ип_4_f4 [3]), .f2(\ип_4_f4 [2]), .f3(\ип_4_f4 [1]),
    .f4(\ип_4_f4 [0]), .f5(\ип_4_f7 [2]), .f6(\ип_4_f7 [1]), .f7(\ип_4_f7 [0]));
  assign controlled_buffer_9_out = not_2_out ? \ИП2  : 4'bz;  // Controlled_Buffer controlled_buffer_12
  not not_2 (not_2_out, L4);
  LED led_1 (.in(\ЗВУК ));
  assign \В2  = and_22_out ? \ип_4_f7  : 3'bz;  // Controlled_Buffer controlled_buffer_13
  assign \В  = and_22_out ? \ип_4_f4  : 4'bz;  // Controlled_Buffer controlled_buffer_14
  assign controlled_buffer_15_out = not_2_out ? \ИП1  : 4'bz;  // Controlled_Buffer controlled_buffer_15
  assign controlled_buffer_15_out = L4 ? \ИП6  : 4'bz;  // Controlled_Buffer controlled_buffer_16
  or u_Q1 (Q1_out, or_1_out, or_2_out);
  or Q1_2 (Q1_2_out, and_3_out, and_4_out, and_5_out);
  or u_Q2 (Q2_out, and_7_out, and_8_out, and_9_out, and_10_out, and_11_out);
  or u_Q3 (Q3_out, and_12_out, and_13_out, and_14_out, and_15_out, and_16_out);
  and i1 (out_8, ~or_1_out, or_2_out, ~L4, ~T2, T3);  // AND_Gate
  and i2 (out_9, ~or_1_out, or_2_out, ~L4, T2, ~T3);  // AND_Gate
  and i3 (out_10, ~or_1_out, or_2_out, ~L4, T2, T3);  // AND_Gate
  and i4 (out_11, ~or_1_out, or_2_out, ~L4, T2, ~T3);  // AND_Gate
  buf i5 (out_12, and_18_out);  // OR_Gate
  or i6 (out_13, and_19_out, and_20_out, and_21_out);
  and i7 (out_14, ~or_1_out, or_2_out, L4, T2);  // AND_Gate
  and and_22 (and_22_out, L2, not_1_out);
  not not_3 (AM, PM);
  assign PM = and_2_out ? \ИП5 [0] : 1'bz;  // Controlled_Buffer controlled_buffer_17
  not not_4 (not_4_out, Q1_out);
  not not_5 (not_5_out, not_4_out);
  D_Flip_Flop \u_Т1  (.clk(not_5_out), .D(Q1_2_out), .Q(L4));  // open: Qn, preset, en, reset
  D_Flip_Flop \u_Т2  (.clk(not_5_out), .D(Q2_out), .Q(T2));  // open: Qn, preset, en, reset
  D_Flip_Flop \u_Т3  (.clk(not_5_out), .D(Q3_out), .Q(T3));  // open: Qn, preset, en, reset
  or or_3 (or_3_out, not_5_out, not_5_out);
  Counter #(.width(4), .max('hf)) counter_2 (.Q(\ИП5 ), .clk(or_4_out), .clr(\КП7ВЫХ ));  // open: load, D, count, carry
  or or_4 (or_4_out, out_10, or_6_out);
  Counter #(.width(4), .max('hf)) counter_3 (.Q(\ИП9 ), .clk(or_9_out), .clr(or_5_out));  // open: load, D, count, carry
  or or_5 (or_5_out, \КП4ВЫХ , out_14);
  D_Flip_Flop \u_Т4  (.clk(or_3_out), .D(L4), .Q(Q1));  // open: Qn, preset, en, reset
  D_Flip_Flop \u_Т5  (.clk(or_3_out), .D(T2), .Q(Q2));  // open: Qn, preset, en, reset
  D_Flip_Flop \u_Т6  (.clk(or_3_out), .D(T3), .Q(Q3));  // open: Qn, preset, en, reset
  Counter #(.width(4), .max('hf)) counter_4 (.Q(\ИП4 ), .clk(or_8_out), .clr(or_6_out));  // open: load, D, count, carry
  or or_6 (or_6_out, \КП6ВЫХ , H);
  or or_7 (or_7_out, out_9, \КП4ВЫХ );
  Counter #(.width(4), .max('hf)) counter_5 (.Q(\ИП3 ), .clk(or_7_out), .clr(or_8_out));  // open: load, D, count, carry
  or or_8 (or_8_out, H, \КП5ВЫХ );
  Counter #(.width(4), .max('hf)) counter_6 (
    .Q(\ИП8 ), .clk(or_10_out), .clr(or_9_out));  // open: load, D, count, carry
  or or_9 (or_9_out, \КП33ВЫХ , out_14);
  Counter #(.width(4), .max('hf)) counter_7 (.Q(\ИП2 ), .clk(\КП3ВЫХ ), .clr(\КП4ВЫХ ));  // open: load, D, count, carry
  not not_6 (not_6_out, in_3);
  Counter #(.width(4), .max('hf)) counter_8 (
    .Q(\ИП7 ), .clk(or_12_out), .clr(or_10_out));  // open: load, D, count, carry
  or or_10 (or_10_out, \КП22ВЫХ , out_14);
  Counter #(.width(4), .max('hf)) counter_9 (
    .Q(\ИП1 ), .clk(or_11_out), .clr(\КП3ВЫХ ));  // open: load, D, count, carry
  or or_11 (or_11_out, out_8, \КП2ВЫХ );
  D_Flip_Flop d_ff_1 (.clk(\КП4ВЫХ ), .D(not_6_out), .Q(\ЗВУК ), .reset(\ВЫХ_СБ ));  // open: Qn, preset, en
  and and_23 (and_23_out, L4, T3);
  and and_24 (and_24_out, L4, T2);
  and and_25 (and_25_out, ~L4, ~T3);  // AND_Gate
  and and_26 (and_26_out, L4, T3);
  and and_27 (and_27_out, L4, T2);
  and and_28 (and_28_out, ~L4, ~T2);  // AND_Gate
  and and_29 (and_29_out, ~L4, ~T2, ~T3);  // AND_Gate
  and and_30 (and_30_out, ~L4, T2, T3);  // AND_Gate
  Counter #(.width(4), .max('hf)) counter_10 (
    .Q(\ИП6 ), .clk(controlled_buffer_18_out), .clr(or_12_out));  // open: load, D, count, carry
  assign controlled_buffer_18_out = L5 ? clock_1_out : 1'bz;  // Controlled_Buffer controlled_buffer_18
  or or_12 (or_12_out, \КП11ВЫХ , out_14);
  or u_L1 (L1, and_23_out, and_24_out, and_25_out);
  or u_L2 (L2, and_26_out, and_27_out, and_28_out);
  or u_L3 (L3, and_29_out, and_30_out);
  and u_L4 (L5, L4, T2, ~T3);  // AND_Gate
  Counter #(.width(4), .max('hf)) counter_11 (
    .Q(\КП2 ), .clk(\КП1ВЫХ ), .clr(\КП2ВЫХ ));  // open: load, D, count, carry
  and and_31 (\ВЫХ_СБ , ~\КП1 [0], ~\КП1 [1], \КП1 [2], ~\КП1 [3]);  // AND_Gate
  Counter #(.width(4), .max('hf)) counter_12 (
    .Q(\КП1 ), .clk(controlled_buffer_19_out), .clr(\КП1ВЫХ ));  // open: load, D, count, carry
  assign controlled_buffer_19_out = not_7_out ? clock_1_out : 1'bz;  // Controlled_Buffer controlled_buffer_19
  Clock clock_1 (.out(clock_1_out));
  Counter #(.width(1), .max('h1)) counter_13 (.Q(counter_13_q), .clk(out_12));  // open: load, D, count, carry, clr
  not not_7 (not_7_out, counter_13_q);
  and and_32 (H, and_37_out, \ИП4 [1]);
  and and_33 (\КП1ВЫХ , ~\КП1 [0], \КП1 [1], ~\КП1 [2], \КП1 [3]);  // AND_Gate
  and and_34 (\КП2ВЫХ , ~\КП2 [0], \КП2 [1], \КП2 [2]);  // AND_Gate
  and and_35 (\КП3ВЫХ , ~\ИП1 [0], \ИП1 [1], ~\ИП1 [2], \ИП1 [3]);  // AND_Gate
  and and_36 (\КП4ВЫХ , ~\ИП2 [0], \ИП2 [1], \ИП2 [2]);  // AND_Gate
  and and_37 (and_37_out, ~\ИП3 [0], ~\ИП3 [1], \ИП3 [2], ~\ИП3 [3]);  // AND_Gate
  and and_38 (\КП6ВЫХ , \ИП4 [0], \ИП4 [1]);
  and and_39 (\КП5ВЫХ , ~\ИП3 [0], \ИП3 [1], ~\ИП3 [2], \ИП3 [3]);  // AND_Gate
  and and_40 (\КП7ВЫХ , ~\ИП5 [0], ~\ИП5 [1], ~\ИП5 [2], \ИП5 [3]);  // AND_Gate
  and and_41 (\КП11ВЫХ , ~\ИП6 [0], \ИП6 [1], ~\ИП6 [2], \ИП6 [3]);  // AND_Gate
  and and_42 (\КП22ВЫХ , ~\ИП7 [0], \ИП7 [1], \ИП7 [2]);  // AND_Gate
  and and_43 (\КП33ВЫХ , ~\ИП8 [0], \ИП8 [1], ~\ИП8 [2], \ИП8 [3]);  // AND_Gate
  and and_44 (\КП44ВЫХ , ~\ИП9 [0], \ИП9 [1], \ИП9 [2]);  // AND_Gate

  // Other names for the same wires on the sheet: i1 = out_8; i2 = out_9; i3 = out_10; i4 = in_5; i5 = out_12;
  //   i6 = out_14; T1 = L4; В9 = AM; В10 = PM; КП3[3:0] = \ИП1 ; КП4[3:0] = \ИП2 ; КП5[3:0] = \ИП3 ; КП6[3:0] = \ИП4 ;
  //   КП7[3:0] = \ИП5 ; КП11[3:0] = \ИП6 ; КП22[3:0] = \ИП7 ; КП33[3:0] = \ИП8 ; КП44[3:0] = \ИП9 

  // Notes on the sheet:
  //   A
  //   B
endmodule

module \ИП  (
  input  a,
  input  b,
  input  c,
  input  d,
  output f1,
  output f2,
  output f3,
  output f4,
  output f5,
  output f6,
  output f7
);

  wire and_1_out, and_2_out, and_3_out, and_4_out, and_5_out, and_6_out, and_7_out, and_8_out, and_9_out,
       and_10_out, and_11_out, and_12_out, and_13_out, and_14_out, and_15_out, and_16_out, not_1_out,
       not_2_out, not_3_out, not_4_out, not_5_out, not_6_out, not_7_out, not_8_out, not_9_out, not_10_out,
       not_11_out, not_12_out, not_13_out, not_14_out, not_15_out, not_16_out, not_17_out, not_18_out,
       not_19_out, not_20_out, not_21_out;

  not not_1 (not_1_out, b);
  and and_1 (and_1_out, not_1_out, c);
  and and_2 (and_2_out, b, not_2_out);
  not not_2 (not_2_out, c);
  and and_3 (and_3_out, b, not_3_out);
  not not_3 (not_3_out, d);
  not not_4 (not_4_out, c);
  and and_4 (and_4_out, not_4_out, not_5_out);
  not not_5 (not_5_out, d);
  and and_5 (and_5_out, b, not_6_out);
  not not_6 (not_6_out, c);
  and and_6 (and_6_out, b, not_7_out);
  not not_7 (not_7_out, d);
  not not_8 (not_8_out, b);
  and and_7 (and_7_out, not_8_out, not_9_out);
  not not_9 (not_9_out, d);
  and and_8 (and_8_out, b, d);
  not not_10 (not_10_out, b);
  not not_11 (not_11_out, c);
  and and_9 (and_9_out, not_11_out, not_12_out);
  not not_12 (not_12_out, d);
  and and_10 (and_10_out, c, d);
  not not_13 (not_13_out, b);
  and and_11 (and_11_out, not_13_out, not_14_out);
  not not_14 (not_14_out, d);
  and and_12 (and_12_out, c, not_15_out);
  not not_15 (not_15_out, d);
  not not_16 (not_16_out, b);
  and and_13 (and_13_out, not_16_out, not_17_out);
  not not_17 (not_17_out, d);
  not not_18 (not_18_out, b);
  and and_14 (and_14_out, not_18_out, c);
  and and_15 (and_15_out, c, not_19_out);
  not not_19 (not_19_out, d);
  and and_16 (and_16_out, b, not_20_out, d);
  not not_20 (not_20_out, c);
  not not_21 (not_21_out, c);
  or or_1 (f7, not_21_out, d, b);
  or or_2 (f1, and_1_out, and_2_out, and_3_out, a);
  or or_3 (f2, and_4_out, and_5_out, and_6_out, a);
  or or_4 (f3, and_7_out, c, and_8_out, a);
  or or_5 (f4, not_10_out, and_9_out, and_10_out);
  or or_6 (f5, and_11_out, and_12_out);
  or or_7 (f6, and_13_out, and_14_out, and_15_out, and_16_out, a);
endmodule

module \секб  (
  input  a,
  input  b,
  output f1
);

  wire not_1_out, not_2_out;

  not not_1 (not_1_out, a);
  and and_1 (f1, not_1_out, not_2_out);
  not not_2 (not_2_out, b);
endmodule
